// Logisim project Group_2_offline_2.circ as structural Verilog: 5 circuits, main circuit FP Adder
module FP_Adder (
  input  [15:0] Number_A,
  input  [15:0] Number_B,
  output Overflow,
  output Underflow,
  output [15:0] Output_Number
);

  wire [3:0] Fraction_Shifter_larger_exponent;
  wire [11:0] Fraction_Shifter_right_shifted_fraction, Fraction_Shifter_unchanged_fraction;
  wire [12:0] Fraction_Adder_fraction_out__13_bit;

  Fraction_Shifter Fraction_Shifter (
    .Sign_Bit_A(Number_A[15]), .Sign_Bit_B(Number_B[15]), .Exponent_A(Number_A[14:11]),
    .Exponent_B(Number_B[14:11]), .Fraction_A(Number_A[10:0]), .Fraction_B(Number_B[10:0]),
    .Output_Sign(Output_Number[15]), .Larger_Exponent(Fraction_Shifter_larger_exponent),
    .Right_Shifted_Fraction(Fraction_Shifter_right_shifted_fraction),
    .Unchanged_Fraction(Fraction_Shifter_unchanged_fraction));  // open: Exponent_Difference
  Fraction_Adder Fraction_Adder (
    .Right_Shifted_Fraction(Fraction_Shifter_right_shifted_fraction),
    .Unchanged_Fraction(Fraction_Shifter_unchanged_fraction), .Sign_Bit_A(Number_A[15]),
    .Sign_Bit_B(Number_B[15]), .Fraction_Out__13_bit(Fraction_Adder_fraction_out__13_bit));
  Normalizer Normalizer (
    .Exponent(Fraction_Shifter_larger_exponent), .Fraction_13_bit(Fraction_Adder_fraction_out__13_bit),
    .Overflow(Overflow), .Underflow(Underflow), .Exponent_out(Output_Number[14:11]),
    .Output_Fraction(Output_Number[10:0]));
endmodule

module Fraction_Shifter (
  input  Sign_Bit_A,
  input  Sign_Bit_B,
  input  [3:0] Exponent_A,
  input  [3:0] Exponent_B,
  input  [10:0] Fraction_A,
  input  [10:0] Fraction_B,
  output Output_Sign,
  output [3:0] Larger_Exponent,
  output [3:0] Exponent_Difference,
  output [11:0] Right_Shifted_Fraction,
  output [11:0] Unchanged_Fraction
);

  wire comparator_1_gt, comparator_1_lt, multiplexer_1_out, multiplexer_2_out, not_1_out, not_2_out;
  wire [3:0] multiplexer_3_out;
  wire [10:0] multiplexer_5_out;

  Comparator #(.width(4), .mode("unsigned")) comparator_1 (
    .a(Exponent_A), .b(Exponent_B), .gt(comparator_1_gt), .lt(comparator_1_lt));  // open: eq
  not not_1 (not_1_out, comparator_1_gt);
  not not_2 (not_2_out, comparator_1_gt);
  Multiplexer #(.enable("false")) multiplexer_1 (
    .in0(Sign_Bit_A), .in1(Sign_Bit_B), .out(multiplexer_1_out), .sel(comparator_1_gt));
  Multiplexer #(.enable("false")) multiplexer_2 (
    .in0(Sign_Bit_A), .in1(Sign_Bit_B), .out(multiplexer_2_out), .sel(not_1_out));
  Multiplexer #(.width(4), .enable("false")) multiplexer_3 (
    .in0(Exponent_A), .in1(Exponent_B), .out(multiplexer_3_out), .sel(comparator_1_gt));
  Multiplexer #(.width(4), .enable("false")) multiplexer_4 (
    .in0(Exponent_A), .in1(Exponent_B), .out(Larger_Exponent), .sel(comparator_1_lt));
  Multiplexer #(.width(11), .enable("false")) multiplexer_5 (
    .in0(Fraction_A), .in1(Fraction_B), .out(multiplexer_5_out), .sel(comparator_1_gt));
  Multiplexer #(.width(11), .enable("false")) multiplexer_6 (
    .in0(Fraction_A), .in1(Fraction_B), .out(Unchanged_Fraction[10:0]), .sel(not_2_out));
  Subtractor #(.width(4)) subtractor_1 (
    .a(Larger_Exponent), .b(multiplexer_3_out), .out(Exponent_Difference), .bin(1'b0));  // open: bout
  Shifter #(.width(12), .shift("lr")) shifter_1 (
    .in({1'b1, multiplexer_5_out}), .\dist (Exponent_Difference), .out(Right_Shifted_Fraction));
  Sign_Bit_Decider Sign_Bit_Decider (
    .Sign_Bit_A(multiplexer_1_out), .Sign_Bit_B(multiplexer_2_out), .Significand_A(Right_Shifted_Fraction),
    .Significand_B({1'b1, Unchanged_Fraction[10:0]}), .Output_Sign(Output_Sign));

  assign Unchanged_Fraction[11] = 1'b1;

  // Notes on the sheet:
  //   4 Bit Comparator
  //   4 Bit Subtractor
  //   12 Bit Shifter
endmodule

module Sign_Bit_Decider (
  input  Sign_Bit_A,
  input  Sign_Bit_B,
  input  [11:0] Significand_A,
  input  [11:0] Significand_B,
  output Output_Sign
);

  wire and_1_out, comparator_1_eq, comparator_1_lt, multiplexer_1_out;

  Comparator #(.width(12), .mode("unsigned")) comparator_1 (
    .a(Significand_A), .b(Significand_B), .eq(comparator_1_eq), .lt(comparator_1_lt));  // open: gt
  Multiplexer #(.enable("false")) multiplexer_1 (
    .in0(Sign_Bit_A), .in1(Sign_Bit_B), .out(multiplexer_1_out), .sel(comparator_1_lt));
  and and_1 (and_1_out, Sign_Bit_A, Sign_Bit_B);
  Multiplexer #(.enable("false")) multiplexer_2 (
    .in0(multiplexer_1_out), .in1(and_1_out), .out(Output_Sign), .sel(comparator_1_eq));

  // Notes on the sheet:
  //   12 Bit Comparator
endmodule

module Fraction_Adder (
  input  [11:0] Right_Shifted_Fraction,
  input  [11:0] Unchanged_Fraction,
  input  Sign_Bit_A,
  input  Sign_Bit_B,
  output [12:0] Fraction_Out__13_bit
);

  wire adder_1_cout, comparator_1_eq, comparator_1_gt, comparator_1_lt, or_1_out, subtractor_1_bout;
  wire [11:0] adder_1_out, and_1_out, and_2_out, and_3_out, and_4_out, multiplexer_1_out, multiplexer_2_out,
       subtractor_1_out;
  wire [11:11] not_1_out, xor_1_out;

  xor xor_1 (xor_1_out[11], Sign_Bit_A, Sign_Bit_B);
  not not_1 (not_1_out[11], xor_1_out[11]);
  assign and_1_out = {12{not_1_out[11]}} & Right_Shifted_Fraction;  // AND_Gate and_1, 12 bits wide
  assign and_2_out = {12{not_1_out[11]}} & Unchanged_Fraction;  // AND_Gate and_2, 12 bits wide
  assign and_3_out = {12{xor_1_out[11]}} & Right_Shifted_Fraction;  // AND_Gate and_3, 12 bits wide
  assign and_4_out = {12{xor_1_out[11]}} & Unchanged_Fraction;  // AND_Gate and_4, 12 bits wide
  Comparator #(.width(12), .mode("unsigned")) comparator_1 (
    .a(and_3_out), .b(and_4_out), .gt(comparator_1_gt), .eq(comparator_1_eq), .lt(comparator_1_lt));
  Multiplexer #(.width(12), .enable("false")) multiplexer_1 (
    .in0(and_3_out), .in1(and_4_out), .out(multiplexer_1_out), .sel(or_1_out));
  or or_1 (or_1_out, comparator_1_eq, comparator_1_lt);
  Multiplexer #(.width(12), .enable("false")) multiplexer_2 (
    .in0(and_3_out), .in1(and_4_out), .out(multiplexer_2_out), .sel(comparator_1_gt));
  Adder #(.width(12)) adder_1 (.a(and_1_out), .b(and_2_out), .out(adder_1_out), .cin(1'b0), .cout(adder_1_cout));
  Subtractor #(.width(12)) subtractor_1 (
    .a(multiplexer_1_out), .b(multiplexer_2_out), .out(subtractor_1_out), .bin(1'b0), .bout(subtractor_1_bout));
  assign Fraction_Out__13_bit[11:0] = adder_1_out | subtractor_1_out;  // OR_Gate or_2, 12 bits wide
  or or_3 (Fraction_Out__13_bit[12], adder_1_cout, subtractor_1_bout);

  // Notes on the sheet:
  //   12 Bit Comparator
  //   12 Bit Full Adder
  //   12 Bit Full Subtractor
endmodule

module Normalizer (
  input  [3:0] Exponent,
  input  [12:0] Fraction_13_bit,
  output Overflow,
  output Underflow,
  output [3:0] Exponent_out,
  output [10:0] Output_Fraction
);

  wire nor_1_out, nor_2_out, not_1_out, not_2_out, or_1_out, priority_encoder_1_gs, subtractor_2_bout;
  wire [3:0] adder_1_out, multiplexer_1_out, multiplexer_2_out, priority_encoder_1_out, subtractor_1_out,
       subtractor_2_out;
  wire [11:0] multiplexer_3_out, shifter_2_out;
  wire [12:0] shifter_1_out;

  nor nor_1 (nor_1_out, Fraction_13_bit[0], Fraction_13_bit[1], Fraction_13_bit[2], Fraction_13_bit[3], Fraction_13_bit[4], Fraction_13_bit[5], Fraction_13_bit[6], Fraction_13_bit[7], Fraction_13_bit[8], Fraction_13_bit[9], Fraction_13_bit[10], Fraction_13_bit[11], Fraction_13_bit[12]);
  Adder #(.width(4)) adder_1 (.a(Exponent), .b(4'b0000), .out(adder_1_out), .cin(1'b1));  // open: cout
  Priority_Encoder #(.select(4)) priority_encoder_1 (
    .in0(Fraction_13_bit[0]), .in1(Fraction_13_bit[1]), .in2(Fraction_13_bit[2]), .in3(Fraction_13_bit[3]),
    .in4(Fraction_13_bit[4]), .in5(Fraction_13_bit[5]), .in6(Fraction_13_bit[6]), .in7(Fraction_13_bit[7]),
    .in8(Fraction_13_bit[8]), .in9(Fraction_13_bit[9]), .in10(Fraction_13_bit[10]),
    .in11(Fraction_13_bit[11]), .in12(1'b0), .in13(1'b0), .in14(1'b0), .in15(1'b0),
    .out(priority_encoder_1_out), .gs(priority_encoder_1_gs), .en_in(1'b1));  // open: en_out
  Shifter #(.width(13), .shift("lr")) shifter_1 (.in(Fraction_13_bit), .\dist (4'b0001), .out(shifter_1_out));
  Subtractor #(.width(4)) subtractor_1 (
    .a(4'b1011), .b(priority_encoder_1_out), .out(subtractor_1_out), .bin(1'b0));  // open: bout
  Multiplexer #(.width(4), .enable("false")) multiplexer_1 (
    .in0(4'b0000), .in1(subtractor_1_out), .out(multiplexer_1_out), .sel(priority_encoder_1_gs));
  Subtractor #(.width(4)) subtractor_2 (
    .a(Exponent), .b(multiplexer_1_out), .out(subtractor_2_out), .bin(1'b0), .bout(subtractor_2_bout));
  Shifter #(.width(12)) shifter_2 (.in(Fraction_13_bit[11:0]), .\dist (multiplexer_1_out), .out(shifter_2_out));
  nor nor_2 (nor_2_out, subtractor_2_out[0], subtractor_2_out[1], subtractor_2_out[2], subtractor_2_out[3]);
  Multiplexer #(.width(4), .enable("false")) multiplexer_2 (
    .in0(subtractor_2_out), .in1(adder_1_out), .out(multiplexer_2_out), .sel(Fraction_13_bit[12]));
  or or_1 (or_1_out, nor_2_out, subtractor_2_bout);
  Multiplexer #(.width(12), .enable("false")) multiplexer_3 (
    .in0(shifter_2_out), .in1(shifter_1_out[11:0]), .out(multiplexer_3_out), .sel(Fraction_13_bit[12]));
  not not_1 (not_1_out, Fraction_13_bit[12]);
  Multiplexer #(.width(4), .disabled(0), .enable("false")) multiplexer_4 (
    .in0(multiplexer_2_out), .in1(4'b0000), .out(Exponent_out), .sel(nor_1_out));
  Multiplexer #(.width(11), .disabled(0), .enable("false")) multiplexer_5 (
    .in0(multiplexer_3_out[10:0]), .in1({11{1'b0}}), .out(Output_Fraction), .sel(nor_1_out));
  not not_2 (not_2_out, nor_1_out);
  and and_1 (Overflow, adder_1_out[0], adder_1_out[1], adder_1_out[3], Fraction_13_bit[12], not_2_out);
  and and_2 (Underflow, or_1_out, not_2_out, not_1_out);

  // Notes on the sheet:
  //   4 Bit Full Adder
  //   13 bit shiter
  //   Priority Encoder
  //   4 Bit Full Subtractor
  //   4 Bit Full Subtractor
  //   13 bit shiter
endmodule
