// Logisim project MIPS_Processor.circ as structural Verilog: 4 circuits, main circuit main
module main (
  input  in_1,
  input  in_2
);

  wire ALU_zf, and_1_out, and_2_out, clock_1_out, Control_Unit_alusrc, Control_Unit_branch_equal,
       Control_Unit_branch_not_equal, Control_Unit_jump, Control_Unit_memread, Control_Unit_memtoreg,
       Control_Unit_memwrite, Control_Unit_regdst, Control_Unit_regwrite, not_1_out, or_1_out;
  wire [2:0] Control_Unit_alu_op;
  wire [3:0] multiplexer_1_out;
  wire [7:0] adder_1_out, adder_2_out, ALU_alu_result, multiplexer_2_out, multiplexer_3_out,
       multiplexer_4_out, multiplexer_5_out, Program_Counter_q, ram_1_data, Register_File_read_data_1,
       Register_File_read_data_2, rom_1_data_2;
  wire [19:0] rom_1_data;

  Clock clock_1 (.out(clock_1_out));
  Register Program_Counter (.D(multiplexer_4_out), .en(in_1), .Q(Program_Counter_q), .clk(clock_1_out), .clr(in_2));
  Adder adder_1 (.a(Program_Counter_q), .b(8'h1), .out(adder_1_out), .cin(1'b0));  // open: cout
  ROM #(.dataWidth(20)) rom_1 (
    .addr(Program_Counter_q), .data({rom_1_data[19:16], rom_1_data_2, rom_1_data[7:0]}));  // open: sel
  Adder adder_2 (.a(adder_1_out), .b(rom_1_data[7:0]), .out(adder_2_out), .cin(1'b0));  // open: cout
  Control_Unit Control_Unit (
    .OPCode(rom_1_data[19:16]), .RegDst(Control_Unit_regdst), .Jump(Control_Unit_jump),
    .Branch_not_Equal(Control_Unit_branch_not_equal), .Branch_Equal(Control_Unit_branch_equal),
    .MemRead(Control_Unit_memread), .MemToReg(Control_Unit_memtoreg), .ALU_Op(Control_Unit_alu_op),
    .MemWrite(Control_Unit_memwrite), .ALUSrc(Control_Unit_alusrc), .RegWrite(Control_Unit_regwrite));
  Multiplexer #(.width(4), .enable("false")) multiplexer_1 (
    .in0(rom_1_data_2[3:0]), .in1(rom_1_data[7:4]), .out(multiplexer_1_out), .sel(Control_Unit_regdst));
  or or_1 (or_1_out, and_1_out, and_2_out);
  and and_1 (and_1_out, Control_Unit_branch_equal, ALU_zf);
  Multiplexer #(.width(8), .enable("false")) multiplexer_2 (
    .in0(adder_1_out), .in1(adder_2_out), .out(multiplexer_2_out), .sel(or_1_out));
  and and_2 (and_2_out, Control_Unit_branch_not_equal, not_1_out);
  not not_1 (not_1_out, ALU_zf);
  Register_File Register_File (
    .Read_Register_1(rom_1_data_2[7:4]), .Read_Register_2(rom_1_data_2[3:0]),
    .Write_Register(multiplexer_1_out), .Write_Data(multiplexer_5_out),
    .Register_Write(Control_Unit_regwrite), .Clock(clock_1_out), .Clear(in_2),
    .Read_Data_1(Register_File_read_data_1), .Read_Data_2(Register_File_read_data_2));
  // Probe on Register_File_read_data_1
  // Probe on Register_File_read_data_2
  Multiplexer #(.width(8), .enable("false")) multiplexer_3 (
    .in0(Register_File_read_data_2), .in1(rom_1_data[7:0]), .out(multiplexer_3_out), .sel(Control_Unit_alusrc));
  _8_bit_ALU ALU (
    .A(Register_File_read_data_1), .B(multiplexer_3_out), .ALUop(Control_Unit_alu_op),
    .ALU_Result(ALU_alu_result), .ZF(ALU_zf));  // open: Carry, Borrow
  Multiplexer #(.width(8), .enable("false")) multiplexer_4 (
    .in0(multiplexer_2_out), .in1(rom_1_data_2), .out(multiplexer_4_out), .sel(Control_Unit_jump));
  // Probe on ALU_alu_result
  RAM #(.bus("separate")) ram_1 (
    .addr(ALU_alu_result), .din(Register_File_read_data_2), .data(ram_1_data), .str(Control_Unit_memwrite),
    .clk(clock_1_out), .ld(Control_Unit_memread), .clr(in_2));  // open: sel
  Multiplexer #(.width(8), .enable("false")) multiplexer_5 (
    .in0(ALU_alu_result), .in1(ram_1_data), .out(multiplexer_5_out), .sel(Control_Unit_memtoreg));

  // Notes on the sheet:
  //   contents of rom_1 (hex, n*v repeats v):
  //   70105 41205 31240 a1401 1900 21052 b5420 52150 85420 62200 f2114 12103 d2203 92021 1800 46601 16200
  //   46601 16100 d6200 76601 d6100 76601 1900 e21f6 46602 16100 d3103 16101 d6100 76601
endmodule

module Control_Unit (
  input  [3:0] OPCode,
  output RegDst,
  output Jump,
  output Branch_not_Equal,
  output Branch_Equal,
  output MemRead,
  output MemToReg,
  output [2:0] ALU_Op,
  output MemWrite,
  output ALUSrc,
  output RegWrite
);

  ROM #(.addrWidth(4), .dataWidth(12)) rom_1 (
    .addr(OPCode),
    .data({RegDst, ALUSrc, MemToReg, RegWrite, MemRead, MemWrite, ALU_Op, Jump, Branch_Equal, Branch_not_Equal}));  // open: sel

  // Notes on the sheet:
  //   Control Words
  //   contents of rom_1 (hex, n*v repeats v):
  //   4 440 d28 900 508 910 518 500 920 d30 a 908 918 780 9 510
endmodule

module Register_File (
  input  [3:0] Read_Register_1,
  input  [3:0] Read_Register_2,
  input  [3:0] Write_Register,
  input  [7:0] Write_Data,
  input  Register_Write,
  input  Clock,
  input  Clear,
  output [7:0] Read_Data_1,
  output [7:0] Read_Data_2
);

  wire decoder_1_out0, decoder_1_out1, decoder_1_out2, decoder_1_out3, decoder_1_out4, decoder_1_out5,
       decoder_1_out6;
  wire [7:0] sp_q, t0_q, t1_q, t2_q, t3_q, t4_q, zero_q;

  Decoder #(.select(3), .disabled(0)) decoder_1 (
    .out0(decoder_1_out0), .out1(decoder_1_out1), .out2(decoder_1_out2), .out3(decoder_1_out3),
    .out4(decoder_1_out4), .out5(decoder_1_out5), .out6(decoder_1_out6), .sel(Write_Register[2:0]),
    .en(Register_Write));  // open: out7
  Register zero (.D({8{1'b0}}), .en(decoder_1_out0), .Q(zero_q), .clk(Clock), .clr(Clear));
  Register t0 (.D(Write_Data), .en(decoder_1_out1), .Q(t0_q), .clk(Clock), .clr(Clear));
  Register t1 (.D(Write_Data), .en(decoder_1_out2), .Q(t1_q), .clk(Clock), .clr(Clear));
  Register t2 (.D(Write_Data), .en(decoder_1_out3), .Q(t2_q), .clk(Clock), .clr(Clear));
  Register t3 (.D(Write_Data), .en(decoder_1_out4), .Q(t3_q), .clk(Clock), .clr(Clear));
  Register t4 (.D(Write_Data), .en(decoder_1_out5), .Q(t4_q), .clk(Clock), .clr(Clear));
  Register sp (.D(Write_Data), .en(decoder_1_out6), .Q(sp_q), .clk(Clock), .clr(Clear));
  Multiplexer #(.select(3), .width(8), .enable("false")) multiplexer_1 (
    .in0(zero_q), .in1(t0_q), .in2(t1_q), .in3(t2_q), .in4(t3_q), .in5(t4_q), .in6(sp_q), .in7({8{1'b0}}),
    .out(Read_Data_1), .sel(Read_Register_1[2:0]));
  // Probe on zero_q
  // Probe on t0_q
  // Probe on t1_q
  // Probe on t2_q
  // Probe on t3_q
  // Probe on t4_q
  // Probe on sp_q
  Multiplexer #(.select(3), .width(8), .enable("false")) multiplexer_2 (
    .in0(zero_q), .in1(t0_q), .in2(t1_q), .in3(t2_q), .in4(t3_q), .in5(t4_q), .in6(sp_q), .in7({8{1'b0}}),
    .out(Read_Data_2), .sel(Read_Register_2[2:0]));
endmodule

module _8_bit_ALU (
  input  [7:0] A,
  input  [7:0] B,
  input  [2:0] ALUop,
  output Carry,
  output Borrow,
  output [7:0] ALU_Result,
  output ZF
);

  wire [7:0] adder_1_out, and_1_out, nor_1_out, or_1_out, shifter_2_out, subtractor_1_out;
  wire [15:0] shifter_1_out;
  wire [15:8] shifter_2_out_2;

  Adder adder_1 (.a(A), .b(B), .out(adder_1_out), .cin(1'b0), .cout(Carry));
  Subtractor subtractor_1 (.a(A), .b(B), .out(subtractor_1_out), .bin(1'b0), .bout(Borrow));
  assign or_1_out = A | B;  // OR_Gate or_1, 8 bits wide
  assign and_1_out = A & B;  // AND_Gate and_1, 8 bits wide
  assign nor_1_out = ~(A | B);  // NOR_Gate nor_1, 8 bits wide
  Shifter #(.width(16)) shifter_1 (.in({{8{1'b0}}, A}), .\dist (B[3:0]), .out(shifter_1_out));
  Shifter #(.width(16), .shift("lr")) shifter_2 (
    .in({{8{1'b0}}, A}), .\dist (B[3:0]), .out({shifter_2_out_2, shifter_2_out}));
  Multiplexer #(.select(3), .width(8), .enable("false")) multiplexer_1 (
    .in0(adder_1_out), .in1(subtractor_1_out), .in2(or_1_out), .in3(and_1_out), .in4(nor_1_out),
    .in5(shifter_1_out[7:0]), .in6(shifter_2_out), .in7({8{1'b0}}), .out(ALU_Result), .sel(ALUop));
  nor nor_2 (ZF, ALU_Result[0], ALU_Result[1], ALU_Result[2], ALU_Result[3], ALU_Result[4], ALU_Result[5], ALU_Result[6], ALU_Result[7]);
endmodule
