// Logisim project MIPS_Processor_r_pipeline_final.circ as structural Verilog: 8 circuits, main circuit main (R pipeline)
module mips_full (
  input  in_1,
  input  in_2
);

  wire ALU_zf, and_1_out, and_2_out, clock_1_out, Control_Unit_alusrc, Control_Unit_branch_equal,
       Control_Unit_branch_not_equal, Control_Unit_jump, Control_Unit_memread, Control_Unit_memtoreg,
       Control_Unit_memwrite, Control_Unit_regdst, Control_Unit_regwrite, not_1_out, or_1_out;
  wire [2:0] Control_Unit_alu_op;
  wire [3:0] multiplexer_1_out;
  wire [7:0] adder_1_out, adder_2_out, ALU_alu_result, multiplexer_2_out, multiplexer_3_out,
       multiplexer_4_out, multiplexer_5_out, Program_Counter_q, ram_1_data, Register_File_read_data_1,
       Register_File_read_data_2, rom_1_data_2;
  wire [19:0] rom_1_data;

  Clock clock_1 (.out(clock_1_out));
  Register Program_Counter (.D(multiplexer_4_out), .en(in_1), .Q(Program_Counter_q), .clk(clock_1_out), .clr(in_2));
  Adder adder_1 (.a(Program_Counter_q), .b(8'h1), .out(adder_1_out), .cin(1'b0));  // open: cout
  ROM #(.dataWidth(20)) rom_1 (
    .addr(Program_Counter_q), .data({rom_1_data[19:16], rom_1_data_2, rom_1_data[7:0]}));  // open: sel
  Adder adder_2 (.a(adder_1_out), .b(rom_1_data[7:0]), .out(adder_2_out), .cin(1'b0));  // open: cout
  Control_Unit Control_Unit (
    .OPCode(rom_1_data[19:16]), .RegDst(Control_Unit_regdst), .Jump(Control_Unit_jump),
    .Branch_not_Equal(Control_Unit_branch_not_equal), .Branch_Equal(Control_Unit_branch_equal),
    .MemRead(Control_Unit_memread), .MemToReg(Control_Unit_memtoreg), .ALU_Op(Control_Unit_alu_op),
    .MemWrite(Control_Unit_memwrite), .ALUSrc(Control_Unit_alusrc), .RegWrite(Control_Unit_regwrite));
  Multiplexer #(.width(4), .enable("false")) multiplexer_1 (
    .in0(rom_1_data_2[3:0]), .in1(rom_1_data[7:4]), .out(multiplexer_1_out), .sel(Control_Unit_regdst));
  or or_1 (or_1_out, and_1_out, and_2_out);
  and and_1 (and_1_out, Control_Unit_branch_equal, ALU_zf);
  Multiplexer #(.width(8), .enable("false")) multiplexer_2 (
    .in0(adder_1_out), .in1(adder_2_out), .out(multiplexer_2_out), .sel(or_1_out));
  and and_2 (and_2_out, Control_Unit_branch_not_equal, not_1_out);
  not not_1 (not_1_out, ALU_zf);
  Register_File Register_File (
    .Read_Register_1(rom_1_data_2[7:4]), .Read_Register_2(rom_1_data_2[3:0]),
    .Write_Register(multiplexer_1_out), .Write_Data(multiplexer_5_out),
    .Register_Write(Control_Unit_regwrite), .Clock(clock_1_out), .Clear(in_2),
    .Read_Data_1(Register_File_read_data_1), .Read_Data_2(Register_File_read_data_2));
  Multiplexer #(.width(8), .enable("false")) multiplexer_3 (
    .in0(Register_File_read_data_2), .in1(rom_1_data[7:0]), .out(multiplexer_3_out), .sel(Control_Unit_alusrc));
  _8_bit_ALU ALU (
    .A(Register_File_read_data_1), .B(multiplexer_3_out), .ALUop(Control_Unit_alu_op),
    .ALU_Result(ALU_alu_result), .ZF(ALU_zf));  // open: Carry, Borrow
  Multiplexer #(.width(8), .enable("false")) multiplexer_4 (
    .in0(multiplexer_2_out), .in1(rom_1_data_2), .out(multiplexer_4_out), .sel(Control_Unit_jump));
  RAM #(.bus("separate")) ram_1 (
    .addr(ALU_alu_result), .din(Register_File_read_data_2), .data(ram_1_data), .str(Control_Unit_memwrite),
    .clk(clock_1_out), .ld(Control_Unit_memread), .clr(in_2));  // open: sel
  Multiplexer #(.width(8), .enable("false")) multiplexer_5 (
    .in0(ALU_alu_result), .in1(ram_1_data), .out(multiplexer_5_out), .sel(Control_Unit_memtoreg));

  // Notes on the sheet:
  //   contents of rom_1 (hex, n*v repeats v):
  //   70105 41205 31240 a1401 1900 21052 b5420 52150 85420 62200 f2114 12103 d2203 92021 1800 46601 16200
  //   46601 16100 d6200 76601 d6100 76601 1900 e21f6 46602 16100 d3103 16101 d6100 76601
endmodule

module Control_Unit (
  input  [3:0] OPCode,
  output RegDst,
  output Jump,
  output Branch_not_Equal,
  output Branch_Equal,
  output MemRead,
  output MemToReg,
  output [2:0] ALU_Op,
  output MemWrite,
  output ALUSrc,
  output RegWrite
);

  ROM #(.addrWidth(4), .dataWidth(12)) rom_1 (
    .addr(OPCode),
    .data({RegDst, ALUSrc, MemToReg, RegWrite, MemRead, MemWrite, ALU_Op, Jump, Branch_Equal, Branch_not_Equal}));  // open: sel

  // Notes on the sheet:
  //   Control Words
  //   contents of rom_1 (hex, n*v repeats v):
  //   4 440 d28 900 508 910 518 500 920 d30 a 908 918 780 9 510
endmodule

module Register_File (
  input  [3:0] Read_Register_1,
  input  [3:0] Read_Register_2,
  input  [3:0] Write_Register,
  input  [7:0] Write_Data,
  input  Register_Write,
  input  Clock,
  input  Clear,
  output [7:0] Read_Data_1,
  output [7:0] Read_Data_2
);

  wire decoder_1_out0, decoder_1_out1, decoder_1_out2, decoder_1_out3, decoder_1_out4, decoder_1_out5,
       decoder_1_out6;
  wire [7:0] sp_q, t0_q, t1_q, t2_q, t3_q, t4_q, zero_q;

  Decoder #(.select(3), .disabled(0)) decoder_1 (
    .out0(decoder_1_out0), .out1(decoder_1_out1), .out2(decoder_1_out2), .out3(decoder_1_out3),
    .out4(decoder_1_out4), .out5(decoder_1_out5), .out6(decoder_1_out6), .sel(Write_Register[2:0]),
    .en(Register_Write));  // open: out7
  Register zero (.D({8{1'b0}}), .en(decoder_1_out0), .Q(zero_q), .clk(Clock), .clr(Clear));
  Register t0 (.D(Write_Data), .en(decoder_1_out1), .Q(t0_q), .clk(Clock), .clr(Clear));
  Register t1 (.D(Write_Data), .en(decoder_1_out2), .Q(t1_q), .clk(Clock), .clr(Clear));
  Register t2 (.D(Write_Data), .en(decoder_1_out3), .Q(t2_q), .clk(Clock), .clr(Clear));
  Register t3 (.D(Write_Data), .en(decoder_1_out4), .Q(t3_q), .clk(Clock), .clr(Clear));
  Register t4 (.D(Write_Data), .en(decoder_1_out5), .Q(t4_q), .clk(Clock), .clr(Clear));
  Register sp (.D(Write_Data), .en(decoder_1_out6), .Q(sp_q), .clk(Clock), .clr(Clear));
  Multiplexer #(.select(3), .width(8), .enable("false")) multiplexer_1 (
    .in0(zero_q), .in1(t0_q), .in2(t1_q), .in3(t2_q), .in4(t3_q), .in5(t4_q), .in6(sp_q), .in7({8{1'b0}}),
    .out(Read_Data_1), .sel(Read_Register_1[2:0]));
  Multiplexer #(.select(3), .width(8), .enable("false")) multiplexer_2 (
    .in0(zero_q), .in1(t0_q), .in2(t1_q), .in3(t2_q), .in4(t3_q), .in5(t4_q), .in6(sp_q), .in7({8{1'b0}}),
    .out(Read_Data_2), .sel(Read_Register_2[2:0]));
endmodule

module _8_bit_ALU (
  input  [7:0] A,
  input  [7:0] B,
  input  [2:0] ALUop,
  output Carry,
  output Borrow,
  output [7:0] ALU_Result,
  output ZF
);

  wire [7:0] adder_1_out, and_1_out, nor_1_out, or_1_out, shifter_2_out, subtractor_1_out;
  wire [15:0] shifter_1_out;
  wire [15:8] shifter_2_out_2;

  Adder adder_1 (.a(A), .b(B), .out(adder_1_out), .cin(1'b0), .cout(Carry));
  Subtractor subtractor_1 (.a(A), .b(B), .out(subtractor_1_out), .bin(1'b0), .bout(Borrow));
  assign or_1_out = A | B;  // OR_Gate or_1, 8 bits wide
  assign and_1_out = A & B;  // AND_Gate and_1, 8 bits wide
  assign nor_1_out = ~(A | B);  // NOR_Gate nor_1, 8 bits wide
  Shifter #(.width(16)) shifter_1 (.in({{8{1'b0}}, A}), .\dist (B[3:0]), .out(shifter_1_out));
  Shifter #(.width(16), .shift("lr")) shifter_2 (
    .in({{8{1'b0}}, A}), .\dist (B[3:0]), .out({shifter_2_out_2, shifter_2_out}));
  Multiplexer #(.select(3), .width(8), .enable("false")) multiplexer_1 (
    .in0(adder_1_out), .in1(subtractor_1_out), .in2(or_1_out), .in3(and_1_out), .in4(nor_1_out),
    .in5(shifter_1_out[7:0]), .in6(shifter_2_out), .in7({8{1'b0}}), .out(ALU_Result), .sel(ALUop));
  nor nor_2 (ZF, ALU_Result[0], ALU_Result[1], ALU_Result[2], ALU_Result[3], ALU_Result[4], ALU_Result[5], ALU_Result[6], ALU_Result[7]);
endmodule

module ReAligned (
  input  in_1,
  input  in_2
);

  wire ALU_zf, and_1_out, and_2_out, clock_1_out, Control_Unit_alusrc, Control_Unit_branch_equal,
       Control_Unit_branch_not_equal, Control_Unit_jump, Control_Unit_memread, Control_Unit_memtoreg,
       Control_Unit_memwrite, Control_Unit_regdst, Control_Unit_regwrite, not_1_out, or_1_out;
  wire [2:0] Control_Unit_alu_op;
  wire [3:0] multiplexer_2_out;
  wire [7:0] adder_1_out, adder_2_out, ALU_alu_result, multiplexer_1_out, multiplexer_3_out,
       multiplexer_4_out, multiplexer_5_out, Program_Counter_q, ram_1_data, Register_File_read_data_1,
       Register_File_read_data_2, rom_1_data_2, rom_1_data_3;
  wire [19:16] rom_1_data;

  Clock clock_1 (.out(clock_1_out));
  Register Program_Counter (.D(multiplexer_4_out), .en(in_1), .Q(Program_Counter_q), .clk(clock_1_out), .clr(in_2));
  Adder adder_1 (.a(Program_Counter_q), .b(8'h1), .out(adder_1_out), .cin(1'b0));  // open: cout
  ROM #(.dataWidth(20)) rom_1 (.addr(Program_Counter_q), .data({rom_1_data, rom_1_data_3, rom_1_data_2}));  // open: sel
  Control_Unit Control_Unit (
    .OPCode(rom_1_data), .RegDst(Control_Unit_regdst), .Jump(Control_Unit_jump),
    .Branch_not_Equal(Control_Unit_branch_not_equal), .Branch_Equal(Control_Unit_branch_equal),
    .MemRead(Control_Unit_memread), .MemToReg(Control_Unit_memtoreg), .ALU_Op(Control_Unit_alu_op),
    .MemWrite(Control_Unit_memwrite), .ALUSrc(Control_Unit_alusrc), .RegWrite(Control_Unit_regwrite));
  Register_File Register_File (
    .Read_Register_1(rom_1_data_3[7:4]), .Read_Register_2(rom_1_data_3[3:0]),
    .Write_Register(multiplexer_2_out), .Write_Data(multiplexer_5_out),
    .Register_Write(Control_Unit_regwrite), .Clock(clock_1_out), .Clear(in_2),
    .Read_Data_1(Register_File_read_data_1), .Read_Data_2(Register_File_read_data_2));
  Multiplexer #(.width(8), .enable("false")) multiplexer_1 (
    .in0(Register_File_read_data_2), .in1(rom_1_data_2), .out(multiplexer_1_out), .sel(Control_Unit_alusrc));
  Multiplexer #(.width(4), .enable("false")) multiplexer_2 (
    .in0(rom_1_data_3[3:0]), .in1(rom_1_data_2[7:4]), .out(multiplexer_2_out), .sel(Control_Unit_regdst));
  Adder adder_2 (.a(adder_1_out), .b(rom_1_data_2), .out(adder_2_out), .cin(1'b0));  // open: cout
  _8_bit_ALU ALU (
    .A(Register_File_read_data_1), .B(multiplexer_1_out), .ALUop(Control_Unit_alu_op),
    .ALU_Result(ALU_alu_result), .ZF(ALU_zf));  // open: Carry, Borrow
  and and_1 (and_1_out, Control_Unit_branch_equal, ALU_zf);
  Multiplexer #(.width(8), .enable("false")) multiplexer_3 (
    .in0(adder_1_out), .in1(adder_2_out), .out(multiplexer_3_out), .sel(or_1_out));
  or or_1 (or_1_out, and_1_out, and_2_out);
  and and_2 (and_2_out, Control_Unit_branch_not_equal, not_1_out);
  not not_1 (not_1_out, ALU_zf);
  Multiplexer #(.width(8), .enable("false")) multiplexer_4 (
    .in0(multiplexer_3_out), .in1(rom_1_data_3), .out(multiplexer_4_out), .sel(Control_Unit_jump));
  RAM #(.bus("separate")) ram_1 (
    .addr(ALU_alu_result), .din(Register_File_read_data_2), .data(ram_1_data), .str(Control_Unit_memwrite),
    .clk(clock_1_out), .ld(Control_Unit_memread), .clr(in_2));  // open: sel
  Multiplexer #(.width(8), .enable("false")) multiplexer_5 (
    .in0(ALU_alu_result), .in1(ram_1_data), .out(multiplexer_5_out), .sel(Control_Unit_memtoreg));

  // Notes on the sheet:
  //   contents of rom_1 (hex, n*v repeats v):
  //   70105 41205 31240 a1401 1900 21052 b5420 52150 85420 62200 f2114 12103 d2203 92021 1800 46601 16200
  //   46601 16100 d6200 76601 d6100 76601 1900 e21f6 46602 16100 d3103 16101 d6100 76601
endmodule

module Pipelined (
  input  in_1,
  input  in_2,
  input  [7:0] in_3,
  input  [19:0] in_4,
  output [7:0] out_5,
  output [19:0] out_6
);

  wire ALU_zf, and_1_out, and_2_out, clock_1_out, clock_2_out, Control_Unit_alusrc,
       Control_Unit_branch_equal, Control_Unit_branch_not_equal, Control_Unit_jump, Control_Unit_memread,
       Control_Unit_memtoreg, Control_Unit_memwrite, Control_Unit_regdst, Control_Unit_regwrite, not_1_out,
       or_1_out;
  wire [2:0] Control_Unit_alu_op;
  wire [3:0] IF_ID_q_2, IF_ID_q_3, IF_ID_q_4, IF_ID_q_5, IF_ID_q_6, multiplexer_2_out;
  wire [7:0] adder_1_out, adder_2_out, ALU_alu_result, IF_ID_q, multiplexer_1_out, multiplexer_3_out,
       multiplexer_4_out, multiplexer_5_out, Program_Counter_q, ram_1_data, Register_File_read_data_1,
       Register_File_read_data_2;
  wire [19:0] rom_1_data;

  Clock clock_1 (.out(clock_1_out));
  Register Program_Counter (.D(multiplexer_4_out), .en(in_1), .Q(Program_Counter_q), .clk(clock_1_out), .clr(in_2));
  Adder adder_1 (.a(Program_Counter_q), .b(8'h1), .out(adder_1_out), .cin(1'b0));  // open: cout
  ROM #(.dataWidth(20)) rom_1 (.addr(Program_Counter_q), .data(rom_1_data));  // open: sel
  Register #(.width(28)) register_1 (.D({in_4, in_3}), .Q({out_6, out_5}), .clk(clock_2_out));  // open: en, clr
  Clock clock_2 (.out(clock_2_out));
  Register #(.width(28)) IF_ID (
    .D({rom_1_data, adder_1_out}), .Q({IF_ID_q_2, IF_ID_q_6, IF_ID_q_5, IF_ID_q_4, IF_ID_q_3, IF_ID_q}),
    .clk(clock_1_out));  // open: en, clr
  Control_Unit Control_Unit (
    .OPCode(IF_ID_q_2), .RegDst(Control_Unit_regdst), .Jump(Control_Unit_jump),
    .Branch_not_Equal(Control_Unit_branch_not_equal), .Branch_Equal(Control_Unit_branch_equal),
    .MemRead(Control_Unit_memread), .MemToReg(Control_Unit_memtoreg), .ALU_Op(Control_Unit_alu_op),
    .MemWrite(Control_Unit_memwrite), .ALUSrc(Control_Unit_alusrc), .RegWrite(Control_Unit_regwrite));
  Register_File Register_File (
    .Read_Register_1(IF_ID_q_6), .Read_Register_2(IF_ID_q_5), .Write_Register(multiplexer_2_out),
    .Write_Data(multiplexer_5_out), .Register_Write(Control_Unit_regwrite), .Clock(clock_1_out),
    .Clear(in_2), .Read_Data_1(Register_File_read_data_1), .Read_Data_2(Register_File_read_data_2));
  Multiplexer #(.width(8), .enable("false")) multiplexer_1 (
    .in0(Register_File_read_data_2), .in1({IF_ID_q_4, IF_ID_q_3}), .out(multiplexer_1_out),
    .sel(Control_Unit_alusrc));
  Multiplexer #(.width(4), .enable("false")) multiplexer_2 (
    .in0(IF_ID_q_5), .in1(IF_ID_q_4), .out(multiplexer_2_out), .sel(Control_Unit_regdst));
  Adder adder_2 (.a(IF_ID_q), .b({IF_ID_q_4, IF_ID_q_3}), .out(adder_2_out), .cin(1'b0));  // open: cout
  _8_bit_ALU ALU (
    .A(Register_File_read_data_1), .B(multiplexer_1_out), .ALUop(Control_Unit_alu_op),
    .ALU_Result(ALU_alu_result), .ZF(ALU_zf));  // open: Carry, Borrow
  and and_1 (and_1_out, Control_Unit_branch_equal, ALU_zf);
  Multiplexer #(.width(8), .enable("false")) multiplexer_3 (
    .in0(IF_ID_q), .in1(adder_2_out), .out(multiplexer_3_out), .sel(or_1_out));
  or or_1 (or_1_out, and_1_out, and_2_out);
  and and_2 (and_2_out, Control_Unit_branch_not_equal, not_1_out);
  not not_1 (not_1_out, ALU_zf);
  Multiplexer #(.width(8), .enable("false")) multiplexer_4 (
    .in0(multiplexer_3_out), .in1({IF_ID_q_6, IF_ID_q_5}), .out(multiplexer_4_out), .sel(Control_Unit_jump));
  RAM #(.bus("separate")) ram_1 (
    .addr(ALU_alu_result), .din(Register_File_read_data_2), .data(ram_1_data), .str(Control_Unit_memwrite),
    .clk(clock_1_out), .ld(Control_Unit_memread), .clr(in_2));  // open: sel
  Multiplexer #(.width(8), .enable("false")) multiplexer_5 (
    .in0(ALU_alu_result), .in1(ram_1_data), .out(multiplexer_5_out), .sel(Control_Unit_memtoreg));

  // Notes on the sheet:
  //   contents of rom_1 (hex, n*v repeats v):
  //   70105 41205 31240 a1401 1900 21052 b5420 52150 85420 62200 f2114 12103 d2203 92021 1800 46601 16200
  //   46601 16100 d6200 76601 d6100 76601 1900 e21f6 46602 16100 d3103 16101 d6100 76601
endmodule

module main__R_pipeline (
  input  in_1,
  input  in_2
);

  wire clock_1_out;
  wire [1:0] Forwarding_unit_forwarda, Forwarding_unit_forwardb;
  wire [2:0] Control_Unit_alu_op;
  wire [4:0] MEM_WB_q;
  wire [7:0] adder_1_out, ALU_alu_result, MEM_WB_q_2, multiplexer_1_out, multiplexer_2_out,
       Program_Counter_q, Register_File_read_data_1;
  wire [12:0] EX_MEM_q;
  wire [19:0] IF_ID_q, rom_1_data;
  wire [31:0] ID_EX_q;
  wire [31:3] Control_Unit_regwrite;

  Clock clock_1 (.out(clock_1_out));
  Adder adder_1 (.a(Program_Counter_q), .b(8'h1), .out(adder_1_out), .cin(1'b0));  // open: cout
  Register Program_Counter (.D(adder_1_out), .en(in_1), .Q(Program_Counter_q), .clk(clock_1_out), .clr(in_2));
  ROM #(.dataWidth(20)) rom_1 (.addr(Program_Counter_q), .data(rom_1_data));  // open: sel
  Register #(.width(20)) IF_ID (
    .D(rom_1_data),
    .Q({IF_ID_q[19:16], Control_Unit_regwrite[27:24], Control_Unit_regwrite[31:28], Control_Unit_regwrite[23:20], IF_ID_q[3:0]}),
    .clk(clock_1_out), .clr(in_2));  // open: en
  Control_Unit Control_Unit (
    .OPCode(IF_ID_q[19:16]), .ALU_Op(Control_Unit_alu_op), .RegWrite(Control_Unit_regwrite[3]));  // open: RegDst, Jump, Branch_not_Equal, Branch_Equal, MemRead, MemToReg, MemWrite, ALUSrc
  Register_File Register_File (
    .Read_Register_1(Control_Unit_regwrite[27:24]), .Read_Register_2(Control_Unit_regwrite[31:28]),
    .Write_Register(MEM_WB_q[4:1]), .Write_Data(MEM_WB_q_2), .Register_Write(MEM_WB_q[0]),
    .Clock(clock_1_out), .Clear(in_2), .Read_Data_1(Register_File_read_data_1),
    .Read_Data_2(Control_Unit_regwrite[19:12]));
  Register #(.width(32)) ID_EX (
    .D({Control_Unit_regwrite[31:12], Register_File_read_data_1, Control_Unit_regwrite[3], Control_Unit_alu_op}),
    .Q(ID_EX_q), .clk(clock_1_out), .clr(in_2));  // open: en
  Forwarding_Unit Forwarding_unit (
    .EX_MEM_regWrite(EX_MEM_q[0]), .MEM_WB_regWrite(MEM_WB_q[0]), .EX_MEM_rd(EX_MEM_q[4:1]),
    .MEM_WB_rd(MEM_WB_q[4:1]), .ID_EX_A(ID_EX_q[27:24]), .ID_EX_B(ID_EX_q[31:28]),
    .ForwardA(Forwarding_unit_forwarda), .ForwardB(Forwarding_unit_forwardb));
  Multiplexer #(.select(2), .width(8)) multiplexer_1 (
    .in0(ID_EX_q[19:12]), .in1(MEM_WB_q_2), .in2(EX_MEM_q[12:5]), .out(multiplexer_1_out),
    .sel(Forwarding_unit_forwardb));  // open: in3, en
  Multiplexer #(.select(2), .width(8)) multiplexer_2 (
    .in0(ID_EX_q[11:4]), .in1(MEM_WB_q_2), .in2(EX_MEM_q[12:5]), .out(multiplexer_2_out),
    .sel(Forwarding_unit_forwarda));  // open: in3, en
  _8_bit_ALU ALU (
    .A(multiplexer_2_out), .B(multiplexer_1_out), .ALUop(ID_EX_q[2:0]), .ALU_Result(ALU_alu_result));  // open: Carry, Borrow, ZF
  Register #(.width(13)) EX_MEM (
    .D({ALU_alu_result, ID_EX_q[23:20], ID_EX_q[3]}), .Q(EX_MEM_q), .clk(clock_1_out), .clr(in_2));  // open: en
  Register #(.width(13)) MEM_WB (.D(EX_MEM_q), .Q({MEM_WB_q_2, MEM_WB_q}), .clk(clock_1_out), .clr(in_2));  // open: en
  RAM #(.bus("separate")) ram_1 (.clk(clock_1_out), .clr(in_2));  // open: addr, din, data, str, sel, ld

  // Notes on the sheet:
  //   contents of rom_1 (hex, n*v repeats v):
  //   70105 41205 31240 a1401 1900 21052 b5420 52150 85420 62200 f2114 12103 d2203 92021 1800 46601 16200
  //   46601 16100 d6200 76601 d6100 76601 1900 e21f6 46602 16100 d3103 16101 d6100 76601
endmodule

module Forwarding_Unit (
  input  EX_MEM_regWrite,
  input  MEM_WB_regWrite,
  input  [3:0] EX_MEM_rd,
  input  [3:0] MEM_WB_rd,
  input  [3:0] ID_EX_A,
  input  [3:0] ID_EX_B,
  output [1:0] ForwardA,
  output [1:0] ForwardB
);

  wire and_3_out, and_4_out, comparator_1_eq, comparator_2_eq, comparator_3_eq, comparator_4_eq, not_1_out,
       not_2_out, or_1_out, or_2_out;

  or or_1 (or_1_out, ID_EX_B[0], ID_EX_B[1], ID_EX_B[2], ID_EX_B[3]);
  or or_2 (or_2_out, ID_EX_A[0], ID_EX_A[1], ID_EX_A[2], ID_EX_A[3]);
  Comparator #(.width(4)) comparator_1 (.a(EX_MEM_rd), .b(ID_EX_A), .eq(comparator_1_eq));  // open: gt, lt
  Comparator #(.width(4)) comparator_2 (.a(EX_MEM_rd), .b(ID_EX_B), .eq(comparator_2_eq));  // open: gt, lt
  Comparator #(.width(4)) comparator_3 (.a(MEM_WB_rd), .b(ID_EX_A), .eq(comparator_3_eq));  // open: gt, lt
  Comparator #(.width(4)) comparator_4 (.a(MEM_WB_rd), .b(ID_EX_B), .eq(comparator_4_eq));  // open: gt, lt
  and and_1 (ForwardA[1], EX_MEM_regWrite, or_2_out, comparator_1_eq);
  and and_2 (ForwardB[1], EX_MEM_regWrite, or_1_out, comparator_2_eq);
  and and_3 (and_3_out, MEM_WB_regWrite, or_2_out, comparator_3_eq);
  and and_4 (and_4_out, MEM_WB_regWrite, or_1_out, comparator_4_eq);
  not not_1 (not_1_out, ForwardA[1]);
  not not_2 (not_2_out, ForwardB[1]);
  and and_5 (ForwardA[0], not_1_out, and_3_out);
  and and_6 (ForwardB[0], not_2_out, and_4_out);
endmodule
